// Logisim project td4_cpu.circ as structural Verilog: 3 circuits, main circuit main
module main (
  input  in_1,
  input  in_2,
  input  in_3,
  input  in_4,
  input  in_5,
  input  in_6,
  input  in_7
);

  wire custom_74hc161_1_qa, custom_74hc161_1_qb, custom_74hc161_1_qc, custom_74hc161_1_qd,
       custom_74hc161_2_qa, custom_74hc161_2_qb, custom_74hc161_2_qc, custom_74hc161_2_qd,
       custom_74hc161_3_qa, custom_74hc161_3_qb, custom_74hc161_3_qc, custom_74hc161_3_qd,
       custom_74hc161_4_qa, custom_74hc161_4_qb, custom_74hc161_4_qc, custom_74hc161_4_qd, multiplexer_1_out,
       multiplexer_2_out, multiplexer_3_out, multiplexer_4_out;

  custom_74HC161 custom_74hc161_1 (
    .A(multiplexer_1_out), .B(multiplexer_2_out), .C(multiplexer_3_out), .D(multiplexer_4_out), .LD(in_1),
    .CK(in_5), .QA(custom_74hc161_1_qa), .QB(custom_74hc161_1_qb), .QC(custom_74hc161_1_qc),
    .QD(custom_74hc161_1_qd));
  custom_74HC161 custom_74hc161_2 (
    .A(multiplexer_1_out), .B(multiplexer_2_out), .C(multiplexer_3_out), .D(multiplexer_4_out), .LD(in_2),
    .CK(in_5), .QA(custom_74hc161_2_qa), .QB(custom_74hc161_2_qb), .QC(custom_74hc161_2_qc),
    .QD(custom_74hc161_2_qd));
  custom_74HC161 custom_74hc161_3 (
    .A(multiplexer_1_out), .B(multiplexer_2_out), .C(multiplexer_3_out), .D(multiplexer_4_out), .LD(in_3),
    .CK(in_5), .QA(custom_74hc161_3_qa), .QB(custom_74hc161_3_qb), .QC(custom_74hc161_3_qc),
    .QD(custom_74hc161_3_qd));
  custom_74HC161 custom_74hc161_4 (
    .A(multiplexer_1_out), .B(multiplexer_2_out), .C(multiplexer_3_out), .D(multiplexer_4_out), .LD(in_4),
    .CK(in_5), .QA(custom_74hc161_4_qa), .QB(custom_74hc161_4_qb), .QC(custom_74hc161_4_qc),
    .QD(custom_74hc161_4_qd));
  Multiplexer #(.select(2)) multiplexer_1 (
    .in0(custom_74hc161_1_qa), .in1(custom_74hc161_2_qa), .in2(custom_74hc161_3_qa),
    .in3(custom_74hc161_4_qa), .out(multiplexer_1_out), .sel({in_7, in_6}));
  Multiplexer #(.select(2)) multiplexer_2 (
    .in0(custom_74hc161_1_qb), .in1(custom_74hc161_2_qb), .in2(custom_74hc161_3_qb),
    .in3(custom_74hc161_4_qb), .out(multiplexer_2_out), .sel({in_7, in_6}));
  Multiplexer #(.select(2)) multiplexer_3 (
    .in0(custom_74hc161_1_qc), .in1(custom_74hc161_2_qc), .in2(custom_74hc161_3_qc),
    .in3(custom_74hc161_4_qc), .out(multiplexer_3_out), .sel({in_7, in_6}));
  Multiplexer #(.select(2)) multiplexer_4 (
    .in0(custom_74hc161_1_qd), .in1(custom_74hc161_2_qd), .in2(custom_74hc161_3_qd),
    .in3(custom_74hc161_4_qd), .out(multiplexer_4_out), .sel({2{in_6}}));
endmodule

module custom_74HC161 (
  input  A,
  input  B,
  input  C,
  input  D,
  input  LD,
  input  CK,
  output QA,
  output QB,
  output QC,
  output QD
);

  wire d_ff_1_qn, multiplexer_1_out, multiplexer_2_out, multiplexer_3_out, multiplexer_4_out, not_1_out;

  Multiplexer multiplexer_1 (.in0(QA), .in1(A), .out(multiplexer_1_out), .sel(not_1_out));
  Multiplexer multiplexer_2 (.in0(QB), .in1(B), .out(multiplexer_2_out), .sel(not_1_out));
  Multiplexer multiplexer_3 (.in0(QC), .in1(C), .out(multiplexer_3_out), .sel(not_1_out));
  Multiplexer multiplexer_4 (.in0(QD), .in1(D), .out(multiplexer_4_out), .sel(not_1_out));
  not not_1 (not_1_out, LD);
  D_Flip_Flop d_ff_1 (.D(multiplexer_1_out), .clk(CK), .Q(QA), .Qn(d_ff_1_qn));  // open: preset, reset
  D_Flip_Flop d_ff_2 (.D(multiplexer_2_out), .clk(CK), .Q(QB));  // open: Qn, preset, reset
  D_Flip_Flop d_ff_3 (.D(multiplexer_3_out), .clk(CK), .Q(QC));  // open: Qn, preset, reset
  D_Flip_Flop d_ff_4 (.D(multiplexer_4_out), .clk(CK), .Q(QD));  // open: Qn, preset, reset
endmodule

module custom_74HC283 (
  input  A1,
  input  B1,
  input  A2,
  input  B2,
  input  A3,
  input  B3,
  input  A4,
  input  B4,
  output S1,
  output S2,
  output S3,
  output S4,
  output C4
);

  wire adder_1_cout, adder_2_cout, adder_3_cout;

  Adder #(.width(1)) adder_1 (.a(A1), .b(B1), .out(S1), .cout(adder_1_cout));  // open: cin
  Adder #(.width(1)) adder_2 (.a(A2), .b(B2), .out(S2), .cin(adder_1_cout), .cout(adder_2_cout));
  Adder #(.width(1)) adder_3 (.a(A3), .b(B3), .out(S3), .cin(adder_2_cout), .cout(adder_3_cout));
  Adder #(.width(1)) adder_4 (.a(A4), .b(B4), .out(S4), .cin(adder_3_cout), .cout(C4));
endmodule
