// Logisim project temp.circ as structural Verilog: 1 circuit, main circuit main
module main (
  input  in_1,
  input  in_2,
  input  in_3,
  input  in_4,
  input  in_5,
  input  in_6,
  input  in_7,
  input  in_8,
  input  in_9,
  input  in_10,
  input  in_11,
  output out_12,
  output out_13,
  output out_14,
  output out_15,
  output out_16
);

  wire and_1_out, and_2_out, and_3_out, and_5_out, d_ff_1_q, d_ff_2_q, multiplexer_1_out, not_1_out,
       not_2_out, not_3_out, xor_2_out;

  not not_1 (not_1_out, d_ff_1_q);
  D_Flip_Flop d_ff_1 (.D(not_1_out), .clk(in_1), .Q(d_ff_1_q));  // open: Qn, preset, reset
  D_Flip_Flop d_ff_2 (.D(multiplexer_1_out), .clk(in_2), .Q(d_ff_2_q));  // open: Qn, preset, reset
  not not_2 (not_2_out, in_6);
  not not_3 (not_3_out, d_ff_2_q);
  and and_1 (and_1_out, in_4, in_6);
  and and_2 (and_2_out, in_5, not_2_out);
  and and_3 (and_3_out, in_10, in_11);
  Multiplexer multiplexer_1 (.in0(d_ff_2_q), .in1(not_3_out), .out(multiplexer_1_out), .sel(in_3));
  or or_1 (out_12, and_1_out, and_2_out);
  xor xor_1 (out_13, in_7, in_8);
  and and_4 (out_14, in_7, in_8);
  xor xor_2 (xor_2_out, in_10, in_11);
  xor xor_3 (out_15, in_9, xor_2_out);
  and and_5 (and_5_out, in_9, xor_2_out);
  or or_2 (out_16, and_5_out, and_3_out);
endmodule
